# Fritzing sketch Untitled Sketch 2 (saved by Fritzing 0.9.2b)
breadboards: 1

parts:
  FRDM-KL25Z1 = FRDM-KL25Z [part_number=FRDM-KL25Z]
  Part1 = WiFi module 8266 [package=2x5-raf]
  Nokia_Display1 = Nokia Display
  R1 = Rotary Potentiometer (Small) [maximum_resistance=100kΩ package=THT]

nets:
  N1: FRDM-KL25Z1.A1_PTB1, Nokia_Display1.RST
  N2: FRDM-KL25Z1.I2C_SDA_PTE0, Part1.2, Part1.4, Part1.6, Part1.8, R1.wiper
  N3: FRDM-KL25Z1.I2C_SCL_PTE1, Part1.1, Part1.3, Part1.5, Part1.7, R1.leg2
  N4: FRDM-KL25Z1.D0_PTA1, Nokia_Display1.GND
  N5: FRDM-KL25Z1.D1_PTA2, Nokia_Display1.BL
  N6: FRDM-KL25Z1.D2_PTD4, Nokia_Display1.VCC
  N7: FRDM-KL25Z1.D3_PTA12_PWM, Nokia_Display1.CLK
  N8: FRDM-KL25Z1.D4_PTA4, Nokia_Display1.DIN
  N9: FRDM-KL25Z1.D5_PTA5_PWM, Nokia_Display1.DC
  N10: FRDM-KL25Z1.D6_PTC8_PWM, Nokia_Display1.CE

custom parts:
  FRDM-KL25Z: Freedom Board, based on basic pinout of Arduino Rev.3. Attention: the board is NOT 5V compatible.
